# Fritzing sketch SerialMonitorArduinoEvery (saved by Fritzing 0.9.3b)
breadboards: 1

parts:
  パーツ1 = Arduino Nano Every
  U1 = LCD-16X2 [package=lcd-16x2_noholes]
  U2 = POT [package=pot_alpha_rv16af-20]

nets:
  N1: パーツ1.RESET, パーツ1.A7
  GND: パーツ1.GND, パーツ1.D13~, U1.VSS, U1.R_W, U1.K, U2.E
  N2: パーツ1.D2, U1.DB7
  N3: パーツ1.D3~, U1.DB6
  N4: パーツ1.D4, U1.DB5
  N5: パーツ1.D5~, U1.DB4
  +5V: パーツ1.D11/MOSI, パーツ1.+5V, U1.VDD, U1.E, U1.A, U2.A
  N6: パーツ1.D12~/MISO, U1.RS
  N7: U1.VO, U2.S

custom parts:
  Arduino Nano Every: The Nano Every is Arduino’s 5V compatible board in the smallest available form factor: 45x18mm! The Arduino Nano is the preferred board for many projects requiring a small and easy to use microcontroller board. The small footprint and low price, make the Nano Every particularly suited for wearable inventions, low cost robotics, electronic musical instruments, and general use to control smaller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
